# Fritzing sketch wiring (saved by Fritzing 0.9.3b)
breadboards: 2

parts:
  LED1 = LED - 5mm [color="Red (633nm)" package="5 mm [THT]"]
  LED2 = LED - 5mm [color="Red (633nm)" package="5 mm [THT]"]
  LED3 = LED - 5mm [color="Red (633nm)" package="5 mm [THT]"]
  LED4 = LED - 5mm [color="Red (633nm)" package="5 mm [THT]"]
  LED5 = LED - 5mm [color="Green (565nm)" package="5 mm [THT]"]
  LED7 = LED - 5mm [color="Green (565nm)" package="5 mm [THT]"]
  R5 = Resistor [tolerance=±5% resistance=220 package=THT]
  R8 = Resistor [tolerance=±5% resistance=220 package=THT]
  Bauteil2 = Arduino Uno (Rev3)
  LED6 = LED - 5mm [color="Green (565nm)" package="5 mm [THT]"]
  LED8 = LED - 5mm [color="Green (565nm)" package="5 mm [THT]"]
  R9 = Resistor [tolerance=±5% resistance=220 package=THT]
  R10 = Resistor [tolerance=±5% resistance=220 package=THT]
  R11 = Resistor [tolerance=±5% resistance=220 package=THT]
  R12 = Resistor [tolerance=±5% resistance=220 package=THT]  # not connected
  R13 = Resistor [tolerance=±5% resistance=220 package=THT]  # not connected
  R14 = Resistor [tolerance=±5% resistance=220 package=THT]
  U2 = 74HC595 [package="DIP16 [THT]"]
  S1 = Momentary Switch [package=ksa_sealed_tac_switch]
  S2 = Momentary Switch [package=ksa_sealed_tac_switch]
  S3 = Momentary Switch [package=ksa_sealed_tac_switch]
  S4 = Momentary Switch [package=ksa_sealed_tac_switch]

nets:
  N1: LED1.cathode, R5.Pin_0
  N2: LED1.anode, U2.Q6
  N3: LED2.anode, U2.Q4
  N4: LED3.anode, U2.Q7
  N5: LED4.cathode, R14.Pin_0
  N6: LED4.anode, U2.Q5
  N7: LED5.cathode, R11.Pin_0
  N8: LED5.anode, U2.Q3
  N9: LED7.cathode, R9.Pin_0
  N10: LED7.anode, U2.Q1
  GND: R5.Pin_1, R8.Pin_1, Bauteil2.GND, R9.Pin_1, R10.Pin_1, R11.Pin_1, R14.Pin_1, U2.GND, U2.OE, S1.1, S1.2, S4.1, S4.2
  N11: R8.Pin_0, LED8.cathode
  N12: Bauteil2.D8, U2.ST_CP
  N13: Bauteil2.D11_PWM/MOSI, U2.DS
  N14: Bauteil2.D12/MISO, U2.SH_CP
  N15: Bauteil2.D2, S1.3, S1.4
  N16: Bauteil2.D3_PWM, S2.3, S2.4
  N17: Bauteil2.D4, S3.3, S3.4
  N18: Bauteil2.D5_PWM, S4.3, S4.4
  5V: Bauteil2.5V, U2.MR, U2.VCC, S2.1, S2.2, S3.1, S3.2
  N19: LED6.cathode, R10.Pin_0
  N20: LED6.anode, U2.Q2
  N21: LED8.anode, U2.Q0
